// Logisim project project.circ as structural Verilog: 17 circuits, main circuit main
module main (
  input  [3:0] in_1,
  output out_2
);

  wire and_1_out, clock_1_out, control_unit_1_dr, control_unit_1_e, control_unit_1_hlt,
       control_unit_1_outr_ld;
  wire [1:0] control_unit_1_ir, control_unit_1_mr;
  wire [2:0] control_unit_1_ar, control_unit_1_pc;
  wire [3:0] alu_4_1_output_ac, control_unit_1_ac, controlled_buffer_1_out, controlled_buffer_1_out_2,
       reg_4_1_output, reg_4_2_output, reg_4_3_output, reg_4_4_output, reg_4_5_output, reg_ir_1_output,
       reg_ir_1_output_2;
  wire [6:0] control_unit_1_alu;
  wire [7:0] ram_1_data;

  Control_Unit control_unit_1 (
    .CLK(and_1_out), .IR_0_4(reg_ir_1_output_2), .HLT(control_unit_1_hlt), .E(control_unit_1_e),
    .MR(control_unit_1_mr), .AR(control_unit_1_ar), .PC(control_unit_1_pc), .DR(control_unit_1_dr),
    .AC(control_unit_1_ac), .OUTR_LD(control_unit_1_outr_ld), .IR(control_unit_1_ir), .ALU(control_unit_1_alu));
  Clock clock_1 (.out(clock_1_out));
  and and_1 (and_1_out, ~control_unit_1_hlt, clock_1_out);  // AND_Gate
  ALU_4 alu_4_1 (
    .AC(reg_4_4_output), .DR(reg_4_3_output), .INPR(in_1), .AND(control_unit_1_alu[0]),
    .ADD(control_unit_1_alu[1]), .COMP(control_unit_1_alu[2]), .DR_LD(control_unit_1_alu[3]),
    .INPR_LD(control_unit_1_alu[4]), .CIR(control_unit_1_alu[5]), .CIL(control_unit_1_alu[6]),
    .CLK(and_1_out), .CLR(control_unit_1_e), .Output_AC(alu_4_1_output_ac), .E(out_2));
  RAM #(.addrWidth(4), .bus("separate")) ram_1 (
    .addr(reg_4_1_output), .din({controlled_buffer_1_out_2, controlled_buffer_1_out}), .data(ram_1_data),
    .str(control_unit_1_mr[1]), .clk(and_1_out));  // open: sel, ld, clr
  reg_4 reg_4_1 (
    .INPUT(controlled_buffer_1_out), .CLK(and_1_out), .LD(control_unit_1_ar[0]), .INC(control_unit_1_ar[2]),
    .OUTPUT(reg_4_1_output));  // open: CLR
  reg_4 reg_4_2 (
    .INPUT(controlled_buffer_1_out), .CLK(and_1_out), .LD(control_unit_1_pc[0]), .INC(control_unit_1_pc[1]),
    .OUTPUT(reg_4_2_output));  // open: CLR
  reg_4 reg_4_3 (
    .INPUT(controlled_buffer_1_out), .CLK(and_1_out), .LD(control_unit_1_dr), .OUTPUT(reg_4_3_output));  // open: INC, CLR
  // Probe on reg_4_4_output
  reg_4 reg_4_4 (
    .INPUT(alu_4_1_output_ac), .CLK(and_1_out), .LD(control_unit_1_ac[0]), .INC(control_unit_1_ac[2]),
    .CLR(control_unit_1_ac[1]), .OUTPUT(reg_4_4_output));
  reg_4 reg_4_5 (
    .INPUT(controlled_buffer_1_out), .CLK(and_1_out), .LD(control_unit_1_outr_ld), .OUTPUT(reg_4_5_output));  // open: INC, CLR
  assign {controlled_buffer_1_out_2, controlled_buffer_1_out} = control_unit_1_mr[0] ? ram_1_data : 8'bz;  // Controlled_Buffer controlled_buffer_1
  // Probe on reg_4_1_output
  // Probe on reg_4_2_output
  // Probe on reg_4_4_output
  // Probe on {reg_ir_1_output_2, reg_ir_1_output}
  reg_IR reg_ir_1 (
    .INPUT({controlled_buffer_1_out_2, controlled_buffer_1_out}), .CLK(and_1_out), .LD(control_unit_1_ir[0]),
    .OUTPUT({reg_ir_1_output_2, reg_ir_1_output}));
  // Probe on reg_4_3_output
  // Probe on reg_4_5_output
  assign {controlled_buffer_1_out_2, controlled_buffer_1_out} = control_unit_1_ar[1] ? {4'b0000, reg_4_1_output} : 8'bz;  // Controlled_Buffer controlled_buffer_2
  assign {controlled_buffer_1_out_2, controlled_buffer_1_out} = control_unit_1_pc[2] ? {4'b0000, reg_4_2_output} : 8'bz;  // Controlled_Buffer controlled_buffer_3
  assign {controlled_buffer_1_out_2, controlled_buffer_1_out} = control_unit_1_ac[3] ? {4'b0000, reg_4_4_output} : 8'bz;  // Controlled_Buffer controlled_buffer_4
  assign {controlled_buffer_1_out_2, controlled_buffer_1_out} = control_unit_1_ir[1] ? {reg_ir_1_output_2, reg_ir_1_output} : 8'bz;  // Controlled_Buffer controlled_buffer_5

  // Notes on the sheet:
  //   AR
  //   PC
  //   DR
  //   AC
  //   OUTR
  //   IR
endmodule

module reg_4 (
  input  INC,
  input  LD,
  input  [3:0] INPUT,
  input  CLK,
  input  CLR,
  output [3:0] OUTPUT
);

  wire and_1_out, and_2_out, and_3_out, and_4_out, and_5_out, and_6_out, and_7_out, and_8_out, and_9_out,
       and_10_out, and_11_out, and_12_out, not_1_out, not_2_out, not_3_out, not_4_out, not_5_out, not_6_out,
       or_1_out, or_2_out, or_3_out, or_4_out, or_5_out, or_6_out, or_7_out, or_8_out;

  not not_1 (not_1_out, LD);
  not not_2 (not_2_out, not_1_out);
  not not_3 (not_3_out, INPUT[0]);
  not not_4 (not_4_out, INPUT[1]);
  not not_5 (not_5_out, INPUT[2]);
  not not_6 (not_6_out, INPUT[3]);
  and and_1 (and_1_out, INC, not_1_out);
  and and_2 (and_2_out, not_2_out, INPUT[0]);
  and and_3 (and_3_out, not_2_out, not_3_out);
  and and_4 (and_4_out, not_2_out, INPUT[1]);
  and and_5 (and_5_out, not_2_out, not_4_out);
  and and_6 (and_6_out, not_2_out, INPUT[2]);
  and and_7 (and_7_out, not_2_out, not_5_out);
  and and_8 (and_8_out, not_2_out, INPUT[3]);
  and and_9 (and_9_out, not_2_out, not_6_out);
  and and_10 (and_10_out, and_1_out, OUTPUT[0]);
  and and_11 (and_11_out, and_1_out, OUTPUT[0], OUTPUT[1]);
  and and_12 (and_12_out, OUTPUT[2], OUTPUT[1], OUTPUT[0], and_1_out);
  or or_1 (or_1_out, and_2_out, and_1_out);
  or or_2 (or_2_out, and_3_out, and_1_out);
  or or_3 (or_3_out, and_4_out, and_10_out);
  or or_4 (or_4_out, and_10_out, and_5_out);
  or or_5 (or_5_out, and_6_out, and_11_out);
  or or_6 (or_6_out, and_11_out, and_7_out);
  or or_7 (or_7_out, and_8_out, and_12_out);
  or or_8 (or_8_out, and_12_out, and_9_out);
  J_K_Flip_Flop j_k_ff_1 (.J(or_1_out), .clk(CLK), .K(or_2_out), .Q(OUTPUT[0]), .reset(CLR));  // open: Qn, preset, en
  J_K_Flip_Flop j_k_ff_2 (.J(or_3_out), .clk(CLK), .K(or_4_out), .Q(OUTPUT[1]), .reset(CLR));  // open: Qn, preset, en
  J_K_Flip_Flop j_k_ff_3 (.J(or_5_out), .clk(CLK), .K(or_6_out), .Q(OUTPUT[2]), .reset(CLR));  // open: Qn, preset, en
  J_K_Flip_Flop j_k_ff_4 (.J(or_7_out), .clk(CLK), .K(or_8_out), .Q(OUTPUT[3]), .reset(CLR));  // open: Qn, preset, en
endmodule

// AC
module ALU_1 (
  input  INPR,
  input  DR,
  input  AC,
  input  AND,
  input  ADD,
  input  Cin,
  input  CMA,
  input  LD_DR,
  input  LD_INPR,
  input  CIR,
  input  CIL,
  input  AC_i_1,
  input  AC_i_1_2,
  output Cout,
  output Output_AC
);

  wire Add_out, adder_1_out, And_out, Comp_out, Id_DR_out, Id_INPR_out, not_1_out, Shl_out, Shr_out;

  Adder #(.width(1)) adder_1 (.a(AC), .b(DR), .out(adder_1_out), .cin(Cin), .cout(Cout));
  not not_1 (not_1_out, AC);
  and u_And (And_out, AND, AC, DR);
  and u_Add (Add_out, ADD, adder_1_out);
  and Comp (Comp_out, CMA, not_1_out);
  and Id_DR (Id_DR_out, LD_DR, DR);
  and Id_INPR (Id_INPR_out, LD_INPR, INPR);
  and Shr (Shr_out, CIR, AC_i_1_2);
  and Shl (Shl_out, CIL, AC_i_1);
  or or_1 (Output_AC, And_out, Add_out, Comp_out, Id_DR_out, Id_INPR_out, Shr_out, Shl_out);
endmodule

// ALU
module ALU_4 (
  input  [3:0] AC,
  input  [3:0] DR,
  input  [3:0] INPR,
  input  AND,
  input  ADD,
  input  COMP,
  input  DR_LD,
  input  INPR_LD,
  input  CIR,
  input  CIL,
  input  CLK,
  input  CLR,
  output [3:0] Output_AC,
  output E
);

  wire alu_1_1_cout, alu_1_2_cout, alu_1_3_cout, alu_1_4_cout, e_1_ac_0_2, e_1_ac_3_2;

  ALU_1 alu_1_1 (
    .AND(AND), .ADD(ADD), .CMA(COMP), .LD_DR(DR_LD), .LD_INPR(INPR_LD), .CIR(CIR), .CIL(CIL),
    .AC_i_1(e_1_ac_0_2), .AC_i_1_2(AC[1]), .INPR(INPR[0]), .DR(DR[0]), .AC(AC[0]), .Cout(alu_1_1_cout),
    .Output_AC(Output_AC[0]));  // open: Cin
  ALU_1 alu_1_2 (
    .AND(AND), .ADD(ADD), .CMA(COMP), .LD_DR(DR_LD), .LD_INPR(INPR_LD), .CIR(CIR), .CIL(CIL), .AC_i_1(AC[0]),
    .AC_i_1_2(AC[2]), .INPR(INPR[1]), .DR(DR[1]), .AC(AC[1]), .Cin(alu_1_1_cout), .Cout(alu_1_2_cout),
    .Output_AC(Output_AC[1]));
  ALU_1 alu_1_3 (
    .AND(AND), .ADD(ADD), .CMA(COMP), .LD_DR(DR_LD), .LD_INPR(INPR_LD), .CIR(CIR), .CIL(CIL), .AC_i_1(AC[1]),
    .AC_i_1_2(AC[3]), .INPR(INPR[2]), .DR(DR[2]), .AC(AC[2]), .Cin(alu_1_2_cout), .Cout(alu_1_3_cout),
    .Output_AC(Output_AC[2]));
  ALU_1 alu_1_4 (
    .AND(AND), .ADD(ADD), .CMA(COMP), .LD_DR(DR_LD), .LD_INPR(INPR_LD), .CIR(CIR), .CIL(CIL), .AC_i_1(AC[2]),
    .AC_i_1_2(e_1_ac_3_2), .INPR(INPR[3]), .DR(DR[3]), .AC(AC[3]), .Cin(alu_1_3_cout), .Cout(alu_1_4_cout),
    .Output_AC(Output_AC[3]));
  E e_1 (
    .ADD(ADD), .Cout(alu_1_4_cout), .AC_0(AC[0]), .CIR(CIL), .AC_3(AC[2]), .CIL(CIR), .CLK(CLK), .CLR(CLR),
    .E(E), .AC_3_2(e_1_ac_3_2), .AC_0_2(e_1_ac_0_2));
endmodule

module reg_IR (
  input  [7:0] INPUT,
  input  CLK,
  input  LD,
  output [7:0] OUTPUT
);

  reg_4 reg_4_1 (.INPUT(INPUT[3:0]), .CLK(CLK), .LD(LD), .OUTPUT(OUTPUT[3:0]));  // open: INC, CLR
  reg_4 reg_4_2 (.INPUT(INPUT[7:4]), .CLK(CLK), .LD(LD), .OUTPUT(OUTPUT[7:4]));  // open: INC, CLR

  // Notes on the sheet:
  //   0-3
  //   4-7
endmodule

// PC
module PC_Control (
  input  T0,
  input  T1,
  input  T3,
  input  T4,
  input  D4,
  input  D5,
  input  D6,
  output PC_LD,
  output PC_INC,
  output PC_BUS
);

  wire AND_2_out, AND_3_out, AND_out, OR_out;

  or OR (OR_out, D6, D4);
  and AND (AND_out, OR_out, T3);
  and AND_2 (AND_2_out, D5, T4);
  and AND_3 (AND_3_out, D5, T3);
  or OR_2 (PC_BUS, AND_3_out, T0);
  or OR_3 (PC_LD, AND_out, AND_2_out);

  assign PC_INC = T1;
endmodule

// Control Unit
module Control_Unit (
  input  CLK,
  input  [3:0] IR_0_4,
  output [1:0] MR,
  output [2:0] AR,
  output [2:0] PC,
  output DR,
  output [3:0] AC,
  output OUTR_LD,
  output [1:0] IR,
  output [6:0] ALU,
  output HLT,
  output E
);

  wire d_ff_1_q, decoder_2_out15, sc_1_clr;
  wire [1:0] decoder_1_out3;
  wire [2:0] decoder_1_out0;
  wire [3:0] counter_1_q;
  wire [14:0] decoder_2_out0;

  SC sc_1 (
    .T3(decoder_1_out3[0]), .T4(decoder_1_out3[1]), .D0(decoder_2_out0[0]), .D1(decoder_2_out0[1]),
    .D2(decoder_2_out0[2]), .D3(decoder_2_out0[3]), .D4(decoder_2_out0[4]), .D5(decoder_2_out0[5]),
    .D6(decoder_2_out0[6]), .D7(decoder_2_out0[7]), .D8(decoder_2_out0[8]), .D9(decoder_2_out0[9]),
    .D10(decoder_2_out0[10]), .D11(decoder_2_out0[11]), .D12(decoder_2_out0[12]), .D13(decoder_2_out0[13]),
    .D14(decoder_2_out0[14]), .CLR(sc_1_clr));
  Decoder #(.select(4)) decoder_1 (
    .out0(decoder_1_out0[0]), .out1(decoder_1_out0[1]), .out2(decoder_1_out0[2]), .out3(decoder_1_out3[0]),
    .out4(decoder_1_out3[1]), .sel(counter_1_q));  // open: out5, out6, out7, out8, out9, out10, out11, out12, out13, out14, out15, en
  Counter #(.width(4), .max('hf)) counter_1 (
    .Q(counter_1_q), .clk(CLK), .clr(d_ff_1_q));  // open: load, D, count, carry
  D_Flip_Flop d_ff_1 (.clk(CLK), .D(sc_1_clr), .Q(d_ff_1_q));  // open: Qn, preset, en, reset
  ALU_Controller alu_controller_1 (
    .T3(decoder_1_out3[0]), .T4(decoder_1_out3[1]), .D0(decoder_2_out0[0]), .D1(decoder_2_out0[1]),
    .D2(decoder_2_out0[2]), .D9(decoder_2_out0[9]), .D11(decoder_2_out0[11]), .D12(decoder_2_out0[12]),
    .D13(decoder_2_out0[13]), .AND(ALU[0]), .ADD(ALU[1]), .COMP(ALU[2]), .DR(ALU[3]), .INPR(ALU[4]),
    .SHR(ALU[5]), .SHL(ALU[6]));
  Decoder #(.select(4)) decoder_2 (
    .out0(decoder_2_out0[0]), .out1(decoder_2_out0[1]), .out2(decoder_2_out0[2]), .out3(decoder_2_out0[3]),
    .out4(decoder_2_out0[4]), .out5(decoder_2_out0[5]), .out6(decoder_2_out0[6]), .out7(decoder_2_out0[7]),
    .out8(decoder_2_out0[8]), .out9(decoder_2_out0[9]), .out10(decoder_2_out0[10]),
    .out11(decoder_2_out0[11]), .out12(decoder_2_out0[12]), .out13(decoder_2_out0[13]),
    .out14(decoder_2_out0[14]), .out15(decoder_2_out15), .sel(IR_0_4));  // open: en
  and and_1 (HLT, decoder_2_out15, decoder_1_out3[0]);
  and and_2 (E, decoder_2_out0[8], decoder_1_out3[0]);
  reg_Controller reg_controller_1 (
    .T0(decoder_1_out0[0]), .T1(decoder_1_out0[1]), .T2(decoder_1_out0[2]), .T3(decoder_1_out3[0]),
    .T4(decoder_1_out3[1]), .D0(decoder_2_out0[0]), .D1(decoder_2_out0[1]), .D2(decoder_2_out0[2]),
    .D3(decoder_2_out0[3]), .D4(decoder_2_out0[4]), .D5(decoder_2_out0[5]), .D6(decoder_2_out0[6]),
    .D7(decoder_2_out0[7]), .D8(decoder_2_out0[8]), .D9(decoder_2_out0[9]), .D10(decoder_2_out0[10]),
    .D11(decoder_2_out0[11]), .D12(decoder_2_out0[12]), .D13(decoder_2_out0[13]), .D14(decoder_2_out0[14]),
    .MR(MR), .AR(AR), .PC(PC), .DR(DR), .AC(AC), .OUTR(OUTR_LD), .IR(IR));  // open: D15

  // Notes on the sheet:
  //   T
  //   D
endmodule

module AR (
  input  T0,
  input  T2,
  input  T3,
  input  T4,
  input  D4,
  input  D5,
  output AR_LD,
  output AR_BUS,
  output AR_INC
);

  wire and_1_out, and_2_out;

  or or_1 (AR_LD, T0, T2);
  and and_1 (and_1_out, D4, T3);
  and and_2 (and_2_out, D5, T4);
  and and_3 (AR_INC, D5, T3);
  or or_2 (AR_BUS, and_1_out, and_2_out);
endmodule

module DR (
  input  T3,
  input  T4,
  input  D0,
  input  D1,
  input  D2,
  output DR_LD,
  output DR_BUS
);

  wire and_1_out, and_2_out, and_3_out, and_4_out, and_5_out;

  and and_1 (and_1_out, D0, T3);
  and and_2 (and_2_out, D1, T3);
  and and_3 (and_3_out, D2, T3);
  and and_4 (and_4_out, D0, T4);
  and and_5 (and_5_out, D1, T4);
  and and_6 (DR_BUS, D2, T4);
  or or_1 (DR_LD, and_1_out, and_2_out, and_3_out, and_4_out, and_5_out);
endmodule

module MR (
  input  T1,
  input  T3,
  input  D0,
  input  D1,
  input  D2,
  input  D3,
  input  D5,
  input  D6,
  output MR_BUS,
  output MR_LD
);

  wire and_1_out, and_2_out, and_3_out, and_4_out, and_5_out, and_6_out;

  and and_1 (and_1_out, D0, T3);
  and and_2 (and_2_out, D1, T3);
  and and_3 (and_3_out, D2, T3);
  and and_4 (and_4_out, D6, T3);
  and and_5 (and_5_out, D3, T3);
  and and_6 (and_6_out, D5, T3);
  or or_1 (MR_BUS, T1, and_1_out, and_2_out, and_3_out, and_4_out);
  or or_2 (MR_LD, and_5_out, and_6_out);
endmodule

module AC (
  input  T3,
  input  T4,
  input  D0,
  input  D1,
  input  D2,
  input  D3,
  input  D7,
  input  D9,
  input  D10,
  input  D11,
  input  D12,
  input  D13,
  input  D14,
  output AC_LD,
  output AC_CLR,
  output AC_INC,
  output AC_BUS
);

  wire and_1_out, and_2_out, and_3_out, and_4_out, and_7_out, and_8_out, COMP_out, SHL_out, SHR_out;

  and and_1 (and_1_out, D0, T4);
  and and_2 (and_2_out, D1, T4);
  and and_3 (and_3_out, D2, T4);
  and COMP (COMP_out, D9, T3);
  and SHL (SHL_out, D11, T3);
  and SHR (SHR_out, D12, T3);
  and and_4 (and_4_out, D13, T3);
  and and_5 (AC_CLR, D7, T3);
  and and_6 (AC_INC, D10, T3);
  and and_7 (and_7_out, D3, T3);
  and and_8 (and_8_out, D14, T3);
  or or_1 (AC_BUS, and_7_out, and_8_out);
  or or_2 (AC_LD, and_1_out, and_2_out, and_3_out, COMP_out, SHL_out, SHR_out, and_4_out);
endmodule

module reg_Controller (
  input  T0,
  input  T1,
  input  T2,
  input  T3,
  input  T4,
  input  D0,
  input  D1,
  input  D2,
  input  D3,
  input  D4,
  input  D5,
  input  D6,
  input  D7,
  input  D8,
  input  D9,
  input  D10,
  input  D11,
  input  D12,
  input  D13,
  input  D14,
  input  D15,
  output [1:0] MR,
  output [2:0] AR,
  output [2:0] PC,
  output DR,
  output [3:0] AC,
  output OUTR,
  output [1:0] IR
);

  MR mr_1 (.T1(T1), .T3(T3), .D0(D0), .D1(D1), .D2(D2), .D3(D3), .D5(D5), .D6(D6), .MR_BUS(MR[0]), .MR_LD(MR[1]));
  AR ar_1 (.T0(T0), .T2(T2), .T3(T3), .T4(T4), .D4(D4), .D5(D5), .AR_LD(AR[0]), .AR_BUS(AR[1]), .AR_INC(AR[2]));
  PC_Control pc_control_1 (
    .T0(T0), .T1(T1), .T3(T3), .T4(T4), .D4(D4), .D5(D5), .D6(D6), .PC_LD(PC[0]), .PC_INC(PC[1]),
    .PC_BUS(PC[2]));
  DR dr_1 (.T3(T3), .T4(T4), .D0(D0), .D1(D1), .D2(D2), .DR_LD(DR));  // open: DR_BUS
  OUTR outr_1 (.D14(D14), .T3(T3), .OUTR_LD(OUTR));
  IR ir_1 (.T1(T1), .T2(T2), .IR_LD(IR[0]), .IR_BUS(IR[1]));
  AC ac_1 (
    .T3(T3), .T4(T4), .D0(D0), .D1(D1), .D2(D2), .D3(D3), .D7(D7), .D9(D9), .D10(D10), .D11(D11), .D12(D12),
    .D13(D13), .D14(D14), .AC_LD(AC[0]), .AC_CLR(AC[1]), .AC_INC(AC[2]), .AC_BUS(AC[3]));
endmodule

module IR (
  input  T1,
  input  T2,
  output IR_LD,
  output IR_BUS
);


  assign IR_BUS = T2;
  assign IR_LD = T1;
endmodule

module OUTR (
  input  D14,
  input  T3,
  output OUTR_LD
);

  and and_1 (OUTR_LD, D14, T3);
endmodule

// ALU_CONTROL
module ALU_Controller (
  input  T3,
  input  T4,
  input  D0,
  input  D1,
  input  D2,
  input  D9,
  input  D11,
  input  D12,
  input  D13,
  output AND,
  output ADD,
  output COMP,
  output DR,
  output INPR,
  output SHR,
  output SHL
);

  and and_1 (AND, D0, T4);
  and and_2 (ADD, D1, T4);
  and and_3 (COMP, D9, T3);
  and and_4 (DR, T4, D2);
  and and_5 (INPR, D13, T3);
  and and_6 (SHR, D11, T3);
  and and_7 (SHL, D12, T3);
endmodule

module SC (
  input  T3,
  input  T4,
  input  D0,
  input  D1,
  input  D2,
  input  D3,
  input  D4,
  input  D5,
  input  D6,
  input  D7,
  input  D8,
  input  D9,
  input  D10,
  input  D11,
  input  D12,
  input  D13,
  input  D14,
  output CLR
);

  wire and_1_out, and_2_out, or_1_out, or_2_out;

  or or_1 (or_1_out, D14, D13, D12, D11, D10, D9, D8, D7, D6, D4, D3);
  or or_2 (or_2_out, D5, D2, D1, D0);
  and and_1 (and_1_out, or_1_out, T3);
  and and_2 (and_2_out, or_2_out, T4);
  or or_3 (CLR, and_1_out, and_2_out);
endmodule

module E (
  input  ADD,
  input  Cout,
  input  AC_0,
  input  CIR,
  input  AC_3,
  input  CIL,
  input  CLK,
  input  CLR,
  output E,
  output AC_3_2,
  output AC_0_2
);

  wire and_1_out, or_1_out;

  and and_1 (and_1_out, ADD, Cout);
  and and_2 (AC_0_2, AC_0, CIR);
  and and_3 (AC_3_2, AC_3, CIL);
  or or_1 (or_1_out, and_1_out, AC_0_2, AC_3_2);
  D_Flip_Flop d_ff_1 (.clk(CLK), .D(or_1_out), .Q(E), .reset(CLR));  // open: Qn, preset, en
endmodule
